# Fritzing sketch Circuit (saved by Fritzing 0.9.6b)

parts:
  R1 = Resistor [tolerance=±5% power=0.25 resistance=220 package=THT]
  LED1 = LED - 5mm [color="Red (633nm)" current=0.030 package="5 mm [THT]"]
  SERVO1 = Adafruit Feedback Servo (small)  # not connected
  Part1 = Arduino Nano (Rev3.0)
  M1 = 1 chan 5v relay module
  JACK1 = 2.1mm Barrel Jack with Terminal Block
  JACK2 = 2.1mm Barrel Jack with Terminal Block
  R5 = Resistor [tolerance=±5% power=0.25 resistance=10k package=THT]
  M2 = DC Motor
  S1 = H-Bridge with L298N

nets:
  N1: R1.Pin_1, Part1.D7
  GND: LED1.cathode, Part1.GND, JACK2.NEG, R5.Pin_0, S1.GND
  N2: Part1.D3, M1.pin_4, R5.Pin_1
  N3: Part1.D5, S1.IN1
  N4: Part1.D6, S1.IN2
  N5: Part1.VIN, JACK2.POS
  5V: Part1.5V, M1.pin_5, S1.5V
  N6: M1.pin_1, JACK1.POS
  N7: M1.pin_2, M1.pin_3, JACK1.NEG
  N8: M2.pin_1, S1.M1-02
  N9: M2.pin_2, S1.M1-01

notes:
  Fan port CN2
  BB lunch port CN10
  Heater - CN5 (G+S to turn on)
  Optionally to CN2 (always on)
  Heater motor
  10k
  220

custom parts:
  Adafruit Feedback Servo (small): Adafruit Feedback Servo (Small)
  1 chan 5v relay module: 1 Channel 5V Relay Module Board Shield with Optocoupler Support High and Low Level Trigger for Arduino.
  H-Bridge with L298N: h-bridge
